# Fritzing sketch Schema (saved by Fritzing 0.9.3b)
breadboards: 1

parts:
  Part1 = Arduino Uno (Rev3)
  Q1 = NPN-Transistor [package="TO92 [THT]"]
  M1 = DC Motor
  R2 = Resistor [tolerance=±5% resistance=220 package=THT]
  YL-83_-_Control_Board1 = richardbruneau00000
  YL-83_-_Detection_Board1 = richardbruneau00000
  Q2 = NPN-Transistor [package="TO92 [THT]"]
  R3 = Resistor [tolerance=±5% resistance=220 package=THT]

nets:
  N1: Part1.D10_PWM/SS, R3.Pin_1
  N2: Part1.D11_PWM/MOSI, R2.Pin_1
  N3: Part1.GND, M1.pin_1, Q2.E
  N4: Part1.D2, YL-83_-_Control_Board1.connector10
  N5: Part1.5V, YL-83_-_Control_Board1.connector8
  N6: Part1.VIN, Q1.E
  N7: Q1.B, R2.Pin_0
  N8: Q1.C, M1.pin_2
  N9: YL-83_-_Control_Board1.connector9, Q2.C
  N10: YL-83_-_Control_Board1.connector12, YL-83_-_Detection_Board1.connector8
  N11: YL-83_-_Control_Board1.connector13, YL-83_-_Detection_Board1.connector9
  N12: Q2.B, R3.Pin_0
